# Fritzing sketch sketch (saved by Fritzing 0.9.3b)

parts:
  Componente1 = Arduino Uno (Rev3)
  Componente2 = Thumb Joystick
  Componente3 = LED Matrix - Serial Interface - Red/Green/Blue
  Componente4 = LED Matrix - Serial Interface - Red/Green/Blue

nets:
  N1: Componente1.A3, Componente2.HORZ
  N2: Componente1.A4/SDA, Componente2.VERT
  N3: Componente1.D10_PWM/SS, Componente3.CS, Componente4.CS
  N4: Componente1.D11_PWM/MOSI, Componente3.MOSI
  N5: Componente1.D13/SCK, Componente3.SCK, Componente4.SCK
  N6: Componente1.D2, Componente2.SW
  N7: Componente1.ioref, Componente2.VCC
  VCC: Componente1.5V, Componente3.VCC, Componente4.VCC
  GND: Componente1.GND, Componente2.SEL, Componente3.GND, Componente4.GND
  N8: Componente3.MISO, Componente4.MOSI

custom parts:
  Thumb Joystick: Description: This is the breakout board for the thumb joystick. Pins are broken out to a 0.1" header and includes 4 mounting holes in the corners. Dimensions: 1" x 1.25"
